// Logisim project 16bit-D-Latch.circ as structural Verilog: 1 circuit, main circuit main
module main (
  input  CLR,
  input  EN,
  input  CLK,
  input  [15:0] IN,
  output [15:0] OUT
);

  D_Flip_Flop d_ff_1 (.clk(CLK), .D(IN[0]), .Q(OUT[0]), .en(CLR), .reset(CLR));  // open: Qn, preset
  D_Flip_Flop d_ff_2 (.clk(CLK), .D(IN[1]), .Q(OUT[1]), .en(CLR), .reset(CLR));  // open: Qn, preset
  D_Flip_Flop d_ff_3 (.clk(CLK), .D(IN[2]), .Q(OUT[2]), .en(CLR), .reset(CLR));  // open: Qn, preset
  D_Flip_Flop d_ff_4 (.clk(CLK), .D(IN[3]), .Q(OUT[3]), .en(CLR), .reset(CLR));  // open: Qn, preset
  D_Flip_Flop d_ff_5 (.clk(CLK), .D(IN[4]), .Q(OUT[4]), .en(CLR), .reset(CLR));  // open: Qn, preset
  D_Flip_Flop d_ff_6 (.clk(CLK), .D(IN[5]), .Q(OUT[5]), .en(CLR), .reset(CLR));  // open: Qn, preset
  D_Flip_Flop d_ff_7 (.clk(CLK), .D(IN[6]), .Q(OUT[6]), .en(CLR), .reset(CLR));  // open: Qn, preset
  D_Flip_Flop d_ff_8 (.clk(CLK), .D(IN[7]), .Q(OUT[7]), .en(CLR), .reset(CLR));  // open: Qn, preset
  D_Flip_Flop d_ff_9 (.clk(CLK), .D(IN[8]), .Q(OUT[8]), .en(CLR), .reset(CLR));  // open: Qn, preset
  D_Flip_Flop d_ff_10 (.clk(CLK), .D(IN[9]), .Q(OUT[9]), .en(CLR), .reset(CLR));  // open: Qn, preset
  D_Flip_Flop d_ff_11 (.clk(CLK), .D(IN[10]), .Q(OUT[10]), .en(CLR), .reset(CLR));  // open: Qn, preset
  D_Flip_Flop d_ff_12 (.clk(CLK), .D(IN[11]), .Q(OUT[11]), .en(CLR), .reset(CLR));  // open: Qn, preset
  D_Flip_Flop d_ff_13 (.clk(CLK), .D(IN[12]), .Q(OUT[12]), .en(CLR), .reset(CLR));  // open: Qn, preset
  D_Flip_Flop d_ff_14 (.clk(CLK), .D(IN[13]), .Q(OUT[13]), .en(CLR), .reset(CLR));  // open: Qn, preset
  D_Flip_Flop d_ff_15 (.clk(CLK), .D(IN[14]), .Q(OUT[14]), .en(CLR), .reset(CLR));  // open: Qn, preset
  D_Flip_Flop d_ff_16 (.clk(CLK), .D(IN[15]), .Q(OUT[15]), .en(CLR), .reset(CLR));  // open: Qn, preset

  assign EN = CLR;
endmodule
