// Logisim project 8bit-D-Latch.circ as structural Verilog: 1 circuit, main circuit main
module main (
  input  CLR,
  input  EN,
  input  CLK,
  input  [7:0] IN,
  output [7:0] OUT
);

  D_Flip_Flop d_ff_1 (.clk(CLK), .D(IN[0]), .Q(OUT[0]), .en(CLR), .reset(CLR));  // open: Qn, preset
  D_Flip_Flop d_ff_2 (.clk(CLK), .D(IN[1]), .Q(OUT[1]), .en(CLR), .reset(CLR));  // open: Qn, preset
  D_Flip_Flop d_ff_3 (.clk(CLK), .D(IN[2]), .Q(OUT[2]), .en(CLR), .reset(CLR));  // open: Qn, preset
  D_Flip_Flop d_ff_4 (.clk(CLK), .D(IN[3]), .Q(OUT[3]), .en(CLR), .reset(CLR));  // open: Qn, preset
  D_Flip_Flop d_ff_5 (.clk(CLK), .D(IN[4]), .Q(OUT[4]), .en(CLR), .reset(CLR));  // open: Qn, preset
  D_Flip_Flop d_ff_6 (.clk(CLK), .D(IN[5]), .Q(OUT[5]), .en(CLR), .reset(CLR));  // open: Qn, preset
  D_Flip_Flop d_ff_7 (.clk(CLK), .D(IN[6]), .Q(OUT[6]), .en(CLR), .reset(CLR));  // open: Qn, preset
  D_Flip_Flop d_ff_8 (.clk(CLK), .D(IN[7]), .Q(OUT[7]), .en(CLR), .reset(CLR));  // open: Qn, preset

  assign EN = CLR;
endmodule
