// Logisim project Project1.circ as structural Verilog: 2 circuits, main circuit main
module main (
  input  [2:0] OutASel,
  input  [2:0] OutBSel,
  input  [3:0] FunSel,
  input  [1:0] FunSel_2,
  input  [3:0] RegSel,
  input  [3:0] TempSel,
  input  [1:0] MuxASel,
  input  [1:0] FunSel_3,
  input  [2:0] RegSel_2,
  input  [1:0] MuxBSel,
  input  in_11,
  input  [1:0] OutCSel,
  input  [1:0] OutDSel,
  input  in_14,
  input  [1:0] FunSel_4,
  output out_16,
  output out_17,
  output out_18,
  output out_19
);

  wire CLK_out;
  wire [3:0] alu_1_zcno;
  wire [7:0] alu_1_outalu, main_2_outa, main_2_outb, main_3_outc, main_3_outd, multiplexer_1_out,
       multiplexer_2_out, ram_1_data;
  wire [15:0] main_1_q;

  Register_16bit_main main_1 (.I(ram_1_data), .FunSel(FunSel_4), .E(in_14), .Q(main_1_q), .CLK(CLK_out), .L_H(in_11));
  Multiplexer #(.select(2), .width(8), .enable("false")) multiplexer_1 (
    .in0(alu_1_outalu), .in1(ram_1_data), .in2(main_1_q[7:0]), .in3(main_3_outc), .out(multiplexer_1_out),
    .sel(MuxASel));
  Part2_main main_2 (
    .Input(multiplexer_1_out), .RegSel(RegSel), .FunSel(FunSel_2), .TempSel(TempSel), .OutASel(OutASel),
    .OutBSel(OutBSel), .OutA(main_2_outa), .OutB(main_2_outb), .in_1(CLK_out));
  Multiplexer #(.select(2), .width(8), .enable("false")) multiplexer_2 (
    .in0(alu_1_outalu), .in1(ram_1_data), .in2(main_1_q[7:0]), .in3(main_3_outc), .out(multiplexer_2_out),
    .sel(MuxBSel));
  Part2_b_main main_3 (
    .Input(multiplexer_2_out), .FunSel(FunSel_3), .RegSel(RegSel_2), .OutCSel(OutCSel), .OutDSel(OutDSel),
    .OutC(main_3_outc), .OutD(main_3_outd), .CLK(CLK_out));
  ALU alu_1 (.A(main_2_outa), .B(main_2_outb), .FunSel(FunSel), .Cin(out_18), .OutALU(alu_1_outalu), .ZCNO(alu_1_zcno));
  ZCNO_Register zcno_register_1 (.ZCNO(alu_1_zcno), .O(out_16), .N(out_17), .C(out_18), .Z(out_19), .CLK(CLK_out));
  Clock CLK (.out(CLK_out));
  RAM #(.bus("separate")) ram_1 (
    .addr(main_3_outd), .din(alu_1_outalu), .data(ram_1_data), .clk(CLK_out));  // open: str, sel, ld, clr

  // Notes on the sheet:
  //   Mux A
  //   Mux B
endmodule

module ZCNO_Register (
  input  [3:0] ZCNO,
  input  CLK,
  output O,
  output N,
  output C,
  output Z
);

  D_Flip_Flop d_ff_1 (.clk(CLK), .D(ZCNO[0]), .Q(O));  // open: Qn, preset, en, reset
  D_Flip_Flop d_ff_2 (.clk(CLK), .D(ZCNO[1]), .Q(N));  // open: Qn, preset, en, reset
  D_Flip_Flop d_ff_3 (.clk(CLK), .D(ZCNO[2]), .Q(C));  // open: Qn, preset, en, reset
  D_Flip_Flop d_ff_4 (.clk(CLK), .D(ZCNO[3]), .Q(Z));  // open: Qn, preset, en, reset
endmodule
