// Logisim project REGISTER - 8 BIT.circ as structural Verilog: 1 circuit, main circuit main
module main (
  input  [7:0] Input,
  input  CLK,
  input  [1:0] FunSel,
  input  EN,
  output [7:0] Output
);

  wire [7:0] adder_1_out, multiplexer_1_out, subtractor_1_out;

  Hex_Digit_Display hex_digit_display_1 (.value(Input[7:4]));  // open: dp
  Hex_Digit_Display hex_digit_display_2 (.value(Input[3:0]));  // open: dp
  Multiplexer #(.select(2), .width(8)) multiplexer_1 (
    .in0(subtractor_1_out), .in1(adder_1_out), .in2(Input), .in3({8{1'b0}}), .out(multiplexer_1_out),
    .sel(FunSel), .en(EN));
  _8bit_D_Latch_main main_1 (.IN(multiplexer_1_out), .CLR(1'b0), .EN(EN), .CLK(CLK), .OUT(Output));
  Adder adder_1 (.a(Output), .b(8'h1), .out(adder_1_out));  // open: cin, cout
  Subtractor subtractor_1 (.a(Output), .b(8'h1), .out(subtractor_1_out));  // open: bin, bout
  Hex_Digit_Display hex_digit_display_3 (.value(Output[7:4]));  // open: dp
  Hex_Digit_Display hex_digit_display_4 (.value(Output[3:0]));  // open: dp

  // Notes on the sheet:
  //   D FLIP FLOP
  //   ADDER
  //   SUBTRACTOR
endmodule
