// Logisim project ALU.circ as structural Verilog: 4 circuits, main circuit ALU
module ALU (
  input  [7:0] A,
  input  [7:0] B,
  input  [3:0] FunSel,
  input  Cin,
  input  OverFlow,
  output [7:0] OutALU,
  output [3:0] ZCNO
);

  wire arithmeticunit_1_cout, arithmeticunit_1_overflow, shiftunit_1_carry_selector, shiftunit_1_out_5;
  wire [7:0] and_1_out, arithmeticunit_1_output, not_1_out, not_2_out, or_1_out, shiftunit_1_outsu, xor_1_out;

  Hex_Digit_Display hex_digit_display_1 (.value(A[3:0]));  // open: dp
  Hex_Digit_Display hex_digit_display_2 (.value(A[7:4]));  // open: dp
  Hex_Digit_Display hex_digit_display_3 (.value(B[7:4]));  // open: dp
  Hex_Digit_Display hex_digit_display_4 (.value(B[3:0]));  // open: dp
  assign and_1_out = A & B;  // AND_Gate and_1, 8 bits wide
  assign or_1_out = A | B;  // OR_Gate or_1, 8 bits wide
  assign xor_1_out = B ^ A;  // XOR_Gate xor_1, 8 bits wide
  ArithmeticUnit arithmeticunit_1 (
    .Carry_In(Cin), .Input_A(A), .Input_B(B), .FunSel(FunSel), .Output(arithmeticunit_1_output),
    .Cout(arithmeticunit_1_cout), .Overflow(arithmeticunit_1_overflow));
  assign not_1_out = ~B;  // NOT_Gate not_1, 8 bits wide
  assign not_2_out = ~A;  // NOT_Gate not_2, 8 bits wide
  ShiftUnit shiftunit_1 (
    .A(A), .Funsel(FunSel), .Carry_Selector(shiftunit_1_carry_selector), .out_5(shiftunit_1_out_5),
    .OutSU(shiftunit_1_outsu));
  Multiplexer #(.select(4), .enable("false")) multiplexer_1 (
    .in0(Cin), .in1(Cin), .in2(Cin), .in3(Cin), .in4(arithmeticunit_1_cout), .in5(arithmeticunit_1_cout),
    .in6(arithmeticunit_1_cout), .in7(Cin), .in8(Cin), .in9(Cin), .in10(shiftunit_1_carry_selector),
    .in11(shiftunit_1_carry_selector), .in12(Cin), .in13(Cin), .in14(shiftunit_1_carry_selector),
    .in15(shiftunit_1_carry_selector), .out(ZCNO[2]), .sel(FunSel));
  Multiplexer #(.select(4), .enable("false")) multiplexer_2 (
    .in0(OverFlow), .in1(OverFlow), .in2(OverFlow), .in3(OverFlow), .in4(arithmeticunit_1_overflow),
    .in5(arithmeticunit_1_overflow), .in6(arithmeticunit_1_overflow), .in7(OverFlow), .in8(OverFlow),
    .in9(OverFlow), .in10(OverFlow), .in11(OverFlow), .in12(shiftunit_1_out_5), .in13(OverFlow),
    .in14(OverFlow), .in15(OverFlow), .out(ZCNO[0]), .sel(FunSel));
  Multiplexer #(.select(4), .width(8), .enable("false")) multiplexer_3 (
    .in0(A), .in1(B), .in2(not_2_out), .in3(not_1_out), .in4(arithmeticunit_1_output),
    .in5(arithmeticunit_1_output), .in6(arithmeticunit_1_output), .in7(and_1_out), .in8(or_1_out),
    .in9(xor_1_out), .in10(shiftunit_1_outsu), .in11(shiftunit_1_outsu), .in12(shiftunit_1_outsu),
    .in13(shiftunit_1_outsu), .in14(shiftunit_1_outsu), .in15(shiftunit_1_outsu), .out(OutALU), .sel(FunSel));
  Hex_Digit_Display hex_digit_display_5 (.value(OutALU[7:4]));  // open: dp
  ZeroChecker zerochecker_1 (.in_1(OutALU), .out_2(ZCNO[3]));
  Hex_Digit_Display hex_digit_display_6 (.value(OutALU[3:0]));  // open: dp

  assign ZCNO[1] = OutALU[7];

  // Notes on the sheet:
  //   A
  //   B
  //   A and B
  //   A or B
  //   Not A
  //   A Xor B
  //   Not B
  //   OutALU
endmodule

module ZeroChecker (
  input  [7:0] in_1,
  output out_2
);

  wire or_1_out;

  or or_1 (or_1_out, in_1[0], in_1[1], in_1[2], in_1[3], in_1[4], in_1[5], in_1[6], in_1[7]);
  not not_1 (out_2, or_1_out);
endmodule

module ShiftUnit (
  input  [7:0] A,
  input  [3:0] Funsel,
  output [7:0] OutSU,
  output Carry_Selector,
  output out_5
);

  wire xor_1_out;

  xor xor_1 (xor_1_out, A[7], A[6]);
  Multiplexer #(.select(3), .width(8), .enable("false")) multiplexer_1 (
    .in0({8{1'b0}}), .in1({8{1'b0}}), .in2({A[6:0], 1'b0}), .in3({1'b0, A[7:1]}), .in4({A[6:0], 1'b0}),
    .in5({{2{A[7]}}, A[6:1]}), .in6({A[6:0], A[7]}), .in7({A[0], A[7:1]}), .out(OutSU), .sel(Funsel[2:0]));
  Multiplexer #(.select(3), .enable("false")) multiplexer_2 (
    .in0(1'b0), .in1(1'b0), .in2(A[7]), .in3(A[0]), .in4(1'b0), .in5(1'b0), .in6(A[7]), .in7(A[0]),
    .out(Carry_Selector), .sel(Funsel[2:0]));
  Multiplexer #(.select(3), .enable("false")) multiplexer_3 (
    .in0(1'b0), .in1(1'b0), .in2(1'b0), .in3(1'b0), .in4(xor_1_out), .in5(1'b0), .in6(1'b0), .in7(1'b0),
    .out(out_5), .sel(Funsel[2:0]));

  // Notes on the sheet:
  //   Logical Shift Left
  //   Logical Shift Right
  //   Arithmetic Shift Left
  //   Arithmetic Shift Right
  //   Circular Shift Left
  //   Circular Shift Right
  //   Overflow Selector
endmodule

module ArithmeticUnit (
  input  [3:0] FunSel,
  input  Carry_In,
  input  [7:0] Input_A,
  input  [7:0] Input_B,
  output [7:0] Output,
  output Cout,
  output Overflow
);

  wire and_1_out, and_2_out, and_3_out, nor_1_out, not_1_out, or_1_out, xor_2_out, xor_3_out;
  wire [7:0] adder_1_out, bit_extender_1_out, xor_1_out;

  assign bit_extender_1_out = {{7{FunSel[1]}}, FunSel[1]};  // Bit_Extender bit_extender_1
  and and_1 (and_1_out, Carry_In, FunSel[0]);
  assign xor_1_out = bit_extender_1_out ^ Input_B;  // XOR_Gate xor_1, 8 bits wide
  xor xor_2 (xor_2_out, Input_A[7], Input_B[7]);
  or or_1 (or_1_out, and_1_out, FunSel[1], FunSel[0]);
  Adder adder_1 (.a(Input_A), .b(xor_1_out), .out(adder_1_out), .cin(or_1_out), .cout(Cout));
  nor nor_1 (nor_1_out, xor_2_out, FunSel[1]);
  xor xor_3 (xor_3_out, Input_B[7], Output[7]);
  not not_1 (not_1_out, xor_3_out);
  and and_2 (and_2_out, nor_1_out, xor_3_out);
  and and_3 (and_3_out, FunSel[1], xor_2_out, not_1_out);
  Multiplexer #(.select(2), .width(8), .enable("false")) multiplexer_1 (
    .in0(adder_1_out), .in1(adder_1_out), .in2(adder_1_out), .out(Output), .sel(FunSel[1:0]));  // open: in3
  or or_2 (Overflow, and_2_out, and_3_out);
endmodule
