// Logisim project As1Part4.circ as structural Verilog: 2 circuits, main circuit main
// 4
module main (
  output out_1,
  output out_2,
  output out_3,
  output out_4
);

  wire CLK_out, EnableIR, EnableRAM, L_H, Read, Write;
  wire [1:0] FunSelARF, FunSelIR, FunSelRF, MuxASel, MuxBSel, OutCSel, OutDSel;
  wire [2:0] OutASel, OutBSel, RegSelARF;
  wire [3:0] alu_1_zcno, FunSelALU, RegSelRF, TempSel;
  wire [7:0] alu_1_outalu, main_2_outa, main_2_outb, main_3_outc, main_3_outd, multiplexer_1_out,
       multiplexer_2_out, ram_1_data;
  wire [15:0] IR;

  Register_16bit_main main_1 (.I(ram_1_data), .FunSel(FunSelIR), .E(EnableIR), .Q(IR), .CLK(CLK_out), .L_H(L_H));
  Multiplexer #(.select(2), .width(8), .enable("false")) multiplexer_1 (
    .in0(alu_1_outalu), .in1(ram_1_data), .in2(IR[7:0]), .in3(main_3_outc), .out(multiplexer_1_out),
    .sel(MuxASel));
  Part2_main main_2 (
    .Input(multiplexer_1_out), .RegSel(RegSelRF), .FunSel(FunSelRF), .TempSel(TempSel), .OutASel(OutASel),
    .OutBSel(OutBSel), .OutA(main_2_outa), .OutB(main_2_outb), .in_1(CLK_out));
  Multiplexer #(.select(2), .width(8), .enable("false")) multiplexer_2 (
    .in0(alu_1_outalu), .in1(ram_1_data), .in2(IR[7:0]), .in3(main_3_outc), .out(multiplexer_2_out),
    .sel(MuxBSel));
  Part2_b_main main_3 (
    .Input(multiplexer_2_out), .FunSel(FunSelARF), .RegSel(RegSelARF), .OutCSel(OutCSel), .OutDSel(OutDSel),
    .OutC(main_3_outc), .OutD(main_3_outd), .CLK(CLK_out));
  ALU alu_1 (
    .A(main_2_outa), .B(main_2_outb), .FunSel(FunSelALU), .Cin(out_2), .OutALU(alu_1_outalu),
    .ZCNO(alu_1_zcno), .OverFlow(out_4));
  ZCNO_Register zcno_register_1 (.ZCNO(alu_1_zcno), .O(out_4), .N(out_3), .C(out_2), .Z(out_1), .CLK(CLK_out));
  Clock CLK (.out(CLK_out));
  RAM #(.bus("separate")) ram_1 (
    .addr(main_3_outd), .din(alu_1_outalu), .data(ram_1_data), .str(Write), .sel(EnableRAM), .clk(CLK_out),
    .ld(Read));  // open: clr
  CU_main main_4 (
    .INSTRUCTION(IR), .OutDSel(OutDSel), .FunSelARF(FunSelARF), .OutBSel(OutBSel), .RegSelARF(RegSelARF),
    .OutCSel(OutCSel), .TempSel(TempSel), .EnableIR(EnableIR), .L_H(L_H), .FunSelIR(FunSelIR),
    .RegSelRF(RegSelRF), .OutASel(OutASel), .FunSel_RF(FunSelRF), .Z(out_1), .EnableRam(EnableRAM),
    .Read(Read), .Write(Write), .MuxASel(MuxASel), .MuxBSel(MuxBSel), .FunSel_ALU(FunSelALU), .in_3(CLK_out));

  // Notes on the sheet:
  //   Mux A
  //   Mux B
endmodule

module ZCNO_Register (
  input  [3:0] ZCNO,
  input  CLK,
  output O,
  output N,
  output C,
  output Z
);

  D_Flip_Flop d_ff_1 (.clk(CLK), .D(ZCNO[0]), .Q(O));  // open: Qn, preset, en, reset
  D_Flip_Flop d_ff_2 (.clk(CLK), .D(ZCNO[1]), .Q(N));  // open: Qn, preset, en, reset
  D_Flip_Flop d_ff_3 (.clk(CLK), .D(ZCNO[2]), .Q(C));  // open: Qn, preset, en, reset
  D_Flip_Flop d_ff_4 (.clk(CLK), .D(ZCNO[3]), .Q(Z));  // open: Qn, preset, en, reset
endmodule
