// Logisim project CU.circ as structural Verilog: 1 circuit, main circuit main
module main (
  input  Z,
  input  [15:0] INSTRUCTION,
  input  in_3,
  output EnableIR,
  output L_H,
  output Read,
  output Write,
  output EnableRam,
  output [1:0] FunSelIR,
  output [1:0] OutDSel,
  output [1:0] FunSelARF,
  output [2:0] OutBSel,
  output [2:0] RegSelARF,
  output [1:0] OutCSel,
  output [3:0] RegSelRF,
  output [2:0] OutASel,
  output [1:0] MuxASel,
  output [1:0] MuxBSel,
  output [3:0] TempSel,
  output [1:0] FunSel_RF,
  output [3:0] FunSel_ALU
);

  wire and_1_out, and_2_out, and_3_out, and_4_out, and_5_out, and_6_out, and_7_out, and_8_out, and_9_out,
       and_10_out, and_11_out, and_12_out, and_13_out, and_14_out, and_15_out, and_16_out, and_17_out,
       and_18_out, and_19_out, and_20_out, and_21_out, and_22_out, and_23_out, and_24_out, and_25_out,
       and_26_out, and_27_out, and_28_out, and_29_out, and_30_out, and_31_out, and_32_out, and_33_out,
       and_34_out, and_35_out, and_36_out, and_37_out, and_38_out, and_39_out, and_40_out, and_41_out,
       and_42_out, and_43_out, and_44_out, and_45_out, and_46_out, and_47_out, and_48_out, and_49_out,
       and_50_out, and_51_out, and_52_out, and_53_out, and_54_out, and_55_out, and_56_out, and_57_out,
       and_58_out, and_59_out, and_60_out, and_61_out, and_62_out, and_63_out, and_64_out, and_65_out,
       and_66_out, and_67_out, and_68_out, and_69_out, and_70_out, and_71_out, and_72_out, and_73_out,
       and_74_out, and_75_out, and_76_out, and_77_out, and_78_out, and_79_out, and_80_out, and_81_out,
       and_82_out, and_83_out, and_84_out, and_85_out, and_86_out, and_87_out, and_88_out, and_89_out,
       and_90_out, and_91_out, and_92_out, and_93_out, and_94_out, and_95_out, and_96_out, and_97_out,
       and_98_out, and_99_out, and_100_out, and_101_out, and_102_out, and_103_out, and_104_out, and_105_out,
       and_106_out, and_107_out, and_108_out, and_109_out, and_110_out, and_111_out, and_112_out,
       and_113_out, and_114_out, and_115_out, and_116_out, and_117_out, and_118_out, and_119_out,
       and_120_out, and_121_out, and_122_out, and_123_out, and_124_out, and_125_out, and_126_out,
       and_127_out, and_128_out, and_129_out, and_130_out, and_131_out, and_132_out, and_133_out,
       and_134_out, and_135_out, and_136_out, and_137_out, and_138_out, and_139_out, and_140_out,
       and_141_out, and_142_out, and_143_out, and_144_out, and_145_out, and_146_out, and_147_out,
       and_148_out, and_149_out, and_150_out, and_151_out, and_152_out, and_153_out, and_154_out,
       and_155_out, and_156_out, and_157_out, and_158_out, and_159_out, and_160_out, and_161_out,
       and_162_out, and_163_out, and_164_out, and_165_out, and_166_out, and_167_out, and_168_out,
       and_169_out, and_170_out, and_171_out, and_172_out, and_173_out, and_174_out, and_175_out,
       and_176_out, and_177_out, and_178_out, and_179_out, and_180_out, and_181_out, and_182_out,
       and_183_out, and_184_out, and_185_out, and_186_out, and_187_out, and_188_out, and_189_out,
       and_190_out, and_191_out, and_192_out, and_193_out, and_194_out, and_195_out, and_196_out,
       and_197_out, and_198_out, and_199_out, and_200_out, and_201_out, and_202_out, and_203_out,
       and_204_out, and_205_out, and_206_out, and_207_out, and_208_out, and_209_out, and_210_out,
       and_211_out, and_212_out, and_213_out, and_214_out, and_215_out, and_216_out, and_217_out,
       and_218_out, and_219_out, and_220_out, and_221_out, and_222_out, and_223_out, and_224_out,
       and_225_out, and_226_out, and_227_out, and_228_out, and_229_out, and_230_out, and_231_out,
       and_232_out, and_233_out, and_234_out, and_235_out, and_236_out, and_237_out, d_ff_1_q,
       decoder_3_out0, decoder_3_out1, decoder_6_out0, decoder_6_out1, decoder_8_out0, decoder_8_out1,
       not_2_out, not_5_out, not_7_out, not_12_out, not_13_out, not_14_out, not_15_out, not_16_out,
       not_17_out, not_18_out, not_19_out, not_20_out, not_21_out, not_22_out, not_23_out, not_24_out,
       not_25_out, not_26_out, not_27_out, not_28_out, not_29_out, not_30_out, not_31_out, not_32_out,
       not_33_out, not_34_out, not_35_out, not_36_out, not_37_out, not_38_out, not_39_out, not_40_out,
       not_41_out, not_42_out, not_43_out, not_44_out, not_45_out, not_46_out, not_47_out, not_48_out,
       not_49_out, not_50_out, not_51_out, not_52_out, not_53_out, not_54_out, not_55_out, not_56_out,
       not_57_out, not_58_out, not_59_out, not_60_out, not_61_out, not_62_out, not_63_out, not_64_out,
       not_65_out, not_66_out, not_67_out, not_68_out, not_69_out, not_70_out, not_71_out, not_72_out,
       not_73_out, not_74_out, not_75_out, not_76_out, not_77_out, not_78_out, not_79_out, not_80_out,
       not_81_out, not_82_out, not_83_out, not_84_out, not_85_out, not_86_out, not_87_out, not_88_out,
       not_89_out, not_90_out, not_91_out, not_92_out, not_93_out, not_94_out, not_95_out, not_96_out,
       not_97_out, not_98_out, not_99_out, not_100_out, not_101_out, not_102_out, not_103_out, not_104_out,
       not_105_out, not_106_out, not_107_out, not_108_out, not_109_out, not_110_out, not_111_out,
       not_112_out, not_113_out, not_114_out, not_115_out, not_116_out, not_117_out, not_118_out,
       not_119_out, not_120_out, not_121_out, not_122_out, not_123_out, not_124_out, not_125_out,
       not_126_out, not_127_out, not_128_out, not_129_out, not_130_out, not_131_out, not_132_out,
       not_133_out, not_134_out, not_135_out, not_136_out, not_137_out, not_138_out, not_139_out,
       not_140_out, not_141_out, not_142_out, not_143_out, not_144_out, not_145_out, not_146_out,
       not_147_out, not_148_out, not_149_out, not_150_out, not_151_out, not_152_out, not_153_out,
       not_154_out, not_155_out, not_156_out, not_157_out, not_158_out, not_159_out, not_160_out,
       not_161_out, not_162_out, not_163_out, not_164_out, not_165_out, not_166_out, not_167_out,
       not_168_out, not_169_out, not_170_out, not_171_out, not_172_out, not_173_out, not_174_out,
       not_175_out, not_176_out, not_177_out, not_178_out, not_179_out, not_180_out, not_181_out,
       not_182_out, not_183_out, not_184_out, not_185_out, not_186_out, not_187_out, not_188_out,
       not_189_out, not_190_out, not_191_out, not_192_out, not_193_out, not_194_out, not_195_out,
       not_196_out, not_197_out, not_198_out, not_199_out, not_200_out, not_201_out, not_202_out,
       not_203_out, not_204_out, not_205_out, not_206_out, not_207_out, not_208_out, not_209_out,
       not_210_out, not_211_out, not_212_out, not_213_out, not_214_out, not_215_out, not_216_out,
       not_217_out, not_218_out, not_219_out, not_220_out, not_221_out, not_222_out, not_223_out,
       not_224_out, not_225_out, not_226_out, not_227_out, not_228_out, not_229_out, not_230_out,
       not_231_out, not_232_out, not_233_out, not_234_out, Opcode0, Opcode1, Opcode2, Opcode3,
       Opcode3_6_9_10, Opcode3_6_9_10_13_14, Opcode4, Opcode4_5, Opcode4_5_7_8, Opcode5, Opcode6,
       Opcode6_9_10, Opcode7, Opcode7_8, Opcode8, Opcode9, Opcode10, Opcode11, Opcode11_12, Opcode12,
       Opcode13, Opcode13_14, Opcode14, Opcode15, or_4_out, or_14_out, or_15_out, or_17_out, or_19_out,
       or_20_out, or_21_out, or_22_out, or_23_out, or_24_out, or_25_out, or_27_out, or_28_out, or_29_out,
       or_30_out, or_31_out, or_32_out, or_33_out, or_34_out, or_35_out, or_36_out, or_37_out, or_38_out,
       or_39_out, or_40_out, or_41_out, or_42_out, or_43_out, or_44_out, or_45_out, or_46_out, or_47_out,
       or_48_out, or_49_out, or_50_out, or_51_out, or_52_out, or_53_out, or_54_out, or_55_out, or_56_out,
       or_57_out, or_58_out, or_59_out, or_60_out, or_61_out, or_62_out, or_63_out, or_64_out, or_65_out,
       or_66_out, or_67_out, or_68_out, or_69_out, Rewind, T0, T1, T2, T3, T4, T5, T6, xor_1_out;
  wire [2:0] counter_1_q, decoder_3_out3, decoder_6_out3, decoder_8_out3, DESTREGARF, SRCREG1ARF, SRCREG2ARF;
  wire [3:0] decoder_2_out3, decoder_4_out3, decoder_7_out3, decoder_9_out3, DESTREGRF, RegSelRF_t,
       SRCREG1RF, SRCREG2RF;

  D_Flip_Flop d_ff_1 (.clk(in_3), .D(Rewind), .Q(d_ff_1_q), .en(1'b1), .reset(d_ff_1_q));  // open: Qn, preset
  Counter #(.width(3), .max('h7)) counter_1 (
    .count(1'b1), .Q(counter_1_q), .clk(in_3), .clr(d_ff_1_q));  // open: load, D, carry
  assign RegSelRF_t = ~decoder_2_out3;  // NOT_Gate not_1, 4 bits wide
  not not_2 (not_2_out, INSTRUCTION[6]);
  assign SRCREG1RF = ~decoder_4_out3;  // NOT_Gate not_3, 4 bits wide
  Decoder #(.select(3), .enable("false")) decoder_1 (
    .out0(T0), .out1(T1), .out2(T2), .out3(T3), .out4(T4), .out5(T5), .out6(T6), .sel(counter_1_q));  // open: out7
  Decoder #(.select(2), .enable("false")) decoder_2 (
    .out0(decoder_2_out3[3]), .out1(decoder_2_out3[2]), .out2(decoder_2_out3[1]), .out3(decoder_2_out3[0]),
    .sel(INSTRUCTION[9:8]));
  Decoder #(.select(2)) decoder_3 (
    .out0(decoder_3_out0), .out1(decoder_3_out1), .out2(decoder_3_out3[1]), .out3(decoder_3_out3[0]),
    .sel(INSTRUCTION[5:4]), .en(not_2_out));
  or or_1 (decoder_3_out3[2], decoder_3_out0, decoder_3_out1);
  Decoder #(.select(2)) decoder_4 (
    .out0(decoder_4_out3[3]), .out1(decoder_4_out3[2]), .out2(decoder_4_out3[1]), .out3(decoder_4_out3[0]),
    .sel(INSTRUCTION[5:4]), .en(INSTRUCTION[6]));
  Decoder #(.select(4)) decoder_5 (
    .out0(Opcode0), .out1(Opcode1), .out2(Opcode2), .out3(Opcode3), .out4(Opcode4), .out5(Opcode5),
    .out6(Opcode6), .out7(Opcode7), .out8(Opcode8), .out9(Opcode9), .out10(Opcode10), .out11(Opcode11),
    .out12(Opcode12), .out13(Opcode13), .out14(Opcode14), .out15(Opcode15), .sel(INSTRUCTION[15:12]));  // open: en
  assign SRCREG1ARF = ~decoder_3_out3;  // NOT_Gate not_4, 3 bits wide
  not not_5 (not_5_out, INSTRUCTION[10]);
  assign DESTREGRF = ~decoder_7_out3;  // NOT_Gate not_6, 4 bits wide
  not not_7 (not_7_out, INSTRUCTION[2]);
  assign SRCREG2RF = ~decoder_9_out3;  // NOT_Gate not_8, 4 bits wide
  Decoder #(.select(2)) decoder_6 (
    .out0(decoder_6_out0), .out1(decoder_6_out1), .out2(decoder_6_out3[1]), .out3(decoder_6_out3[0]),
    .sel(INSTRUCTION[9:8]), .en(not_5_out));
  or or_2 (decoder_6_out3[2], decoder_6_out0, decoder_6_out1);
  Decoder #(.select(2)) decoder_7 (
    .out0(decoder_7_out3[3]), .out1(decoder_7_out3[2]), .out2(decoder_7_out3[1]), .out3(decoder_7_out3[0]),
    .sel(INSTRUCTION[9:8]), .en(INSTRUCTION[10]));
  Decoder #(.select(2)) decoder_8 (
    .out0(decoder_8_out0), .out1(decoder_8_out1), .out2(decoder_8_out3[1]), .out3(decoder_8_out3[0]),
    .sel(INSTRUCTION[1:0]), .en(not_7_out));
  or or_3 (decoder_8_out3[2], decoder_8_out0, decoder_8_out1);
  Decoder #(.select(2)) decoder_9 (
    .out0(decoder_9_out3[3]), .out1(decoder_9_out3[2]), .out2(decoder_9_out3[1]), .out3(decoder_9_out3[0]),
    .sel(INSTRUCTION[1:0]), .en(INSTRUCTION[2]));
  assign DESTREGARF = ~decoder_6_out3;  // NOT_Gate not_9, 3 bits wide
  assign SRCREG2ARF = ~decoder_8_out3;  // NOT_Gate not_10, 3 bits wide
  assign L_H = T0 ? 1'b1 : 1'bz;  // Controlled_Buffer controlled_buffer_1
  assign L_H = T2 ? 1'b0 : 1'bz;  // Controlled_Buffer controlled_buffer_2
  or or_4 (or_4_out, T0, T2);
  or or_5 (EnableIR, T0, T2);
  assign FunSelIR = or_4_out ? 2'b10 : 2'bz;  // Controlled_Buffer controlled_buffer_3
  or or_6 (Opcode13_14, Opcode13, Opcode14);
  or or_7 (Opcode4_5, Opcode4, Opcode5);
  or or_8 (Opcode7_8, Opcode7, Opcode8);
  or or_9 (Opcode11_12, Opcode11, Opcode12);
  or or_10 (Opcode4_5_7_8, Opcode4, Opcode5, Opcode7, Opcode8);
  or or_11 (Opcode6_9_10, Opcode6, Opcode9, Opcode10);
  or or_12 (Opcode3_6_9_10, Opcode6, Opcode9, Opcode3, Opcode10);
  or or_13 (Opcode3_6_9_10_13_14, Opcode6, Opcode9, Opcode3, Opcode10, Opcode13, Opcode14);
  and and_1 (and_1_out, Opcode12, T4);
  and and_2 (and_2_out, Opcode2, T4);
  and and_3 (and_3_out, Opcode1, T4);
  and and_4 (and_4_out, Opcode11, T5);
  or or_14 (or_14_out, and_1_out, and_2_out);
  or or_15 (or_15_out, T0, T2, and_3_out, and_4_out);
  assign Read = or_15_out ? 1'b1 : 1'bz;  // Controlled_Buffer controlled_buffer_4
  or or_16 (EnableRam, or_14_out, or_15_out);
  assign Read = or_14_out ? 1'b0 : 1'bz;  // Controlled_Buffer controlled_buffer_5
  not not_11 (Write, Read);
  and and_5 (and_5_out, INSTRUCTION[2], INSTRUCTION[6]);
  xor xor_1 (xor_1_out, INSTRUCTION[2], INSTRUCTION[6]);
  not not_12 (not_12_out, INSTRUCTION[2]);
  not not_13 (not_13_out, INSTRUCTION[6]);
  and and_6 (and_6_out, Opcode13_14, T6);
  and and_7 (and_7_out, not_12_out, not_13_out);
  not not_14 (not_14_out, INSTRUCTION[6]);
  or or_17 (or_17_out, Opcode0, Opcode1, Opcode2, Opcode3, Opcode12, Opcode15);
  and and_8 (and_8_out, or_17_out, T4);
  and and_9 (and_9_out, Opcode11, T5);
  and and_10 (and_10_out, Opcode4_5_7_8, and_5_out, T4);
  and and_11 (and_11_out, Opcode4_5_7_8, xor_1_out, T5);
  and and_12 (and_12_out, Opcode4_5_7_8, and_7_out, T6);
  and and_13 (and_13_out, INSTRUCTION[6], Opcode6_9_10, T4);
  and and_14 (and_14_out, not_14_out, Opcode6_9_10, T5);
  or or_18 (Rewind, and_11_out, and_8_out, and_9_out, and_10_out, and_12_out, and_13_out, and_14_out, and_6_out);
  not not_15 (not_15_out, INSTRUCTION[10]);
  not not_16 (not_16_out, INSTRUCTION[6]);
  not not_17 (not_17_out, INSTRUCTION[2]);
  not not_18 (not_18_out, INSTRUCTION[10]);
  not not_19 (not_19_out, INSTRUCTION[6]);
  not not_20 (not_20_out, INSTRUCTION[2]);
  not not_21 (not_21_out, INSTRUCTION[2]);
  not not_22 (not_22_out, INSTRUCTION[6]);
  not not_23 (not_23_out, INSTRUCTION[6]);
  not not_24 (not_24_out, INSTRUCTION[10]);
  not not_25 (not_25_out, INSTRUCTION[6]);
  not not_26 (not_26_out, INSTRUCTION[6]);
  not not_27 (not_27_out, INSTRUCTION[10]);
  not not_28 (not_28_out, INSTRUCTION[6]);
  and and_15 (and_15_out, Opcode13_14, INSTRUCTION[6], T4, not_15_out);
  and and_16 (and_16_out, Opcode13_14, not_16_out, T6, INSTRUCTION[10]);
  not not_29 (not_29_out, INSTRUCTION[6]);
  not not_30 (not_30_out, INSTRUCTION[10]);
  not not_31 (not_31_out, INSTRUCTION[2]);
  not not_32 (not_32_out, INSTRUCTION[6]);
  not not_33 (not_33_out, INSTRUCTION[10]);
  not not_34 (not_34_out, INSTRUCTION[2]);
  not not_35 (not_35_out, INSTRUCTION[6]);
  not not_36 (not_36_out, INSTRUCTION[2]);
  not not_37 (not_37_out, INSTRUCTION[6]);
  not not_38 (not_38_out, INSTRUCTION[10]);
  and and_17 (and_17_out, Opcode4_5_7_8, T4, INSTRUCTION[2], not_30_out, not_29_out);
  and and_18 (and_18_out, Opcode4_5_7_8, T4, not_17_out, not_18_out, INSTRUCTION[6]);
  and and_19 (and_19_out, Opcode4_5_7_8, T4, INSTRUCTION[2], INSTRUCTION[10], not_19_out);
  and and_20 (and_20_out, Opcode4_5_7_8, T4, not_20_out, INSTRUCTION[10], INSTRUCTION[6]);
  and and_21 (and_21_out, Opcode4_5_7_8, T4, not_21_out, INSTRUCTION[10], not_22_out);
  and and_22 (and_22_out, Opcode4_5_7_8, T4, not_31_out, not_33_out, not_32_out);
  and and_23 (and_23_out, Opcode4_5_7_8, T5, not_34_out, INSTRUCTION[10], not_35_out);
  and and_24 (and_24_out, Opcode4_5_7_8, T5, not_36_out, not_38_out, not_37_out);
  and and_25 (and_25_out, Opcode6_9_10, not_23_out, T4, not_24_out);
  and and_26 (and_26_out, Opcode3_6_9_10, not_25_out, T4, INSTRUCTION[10]);
  and and_27 (and_27_out, Opcode13_14, not_26_out, T4, not_27_out);
  and and_28 (and_28_out, Opcode13_14, not_28_out, T4, INSTRUCTION[10]);
  not not_39 (not_39_out, INSTRUCTION[2]);
  not not_40 (not_40_out, INSTRUCTION[6]);
  not not_41 (not_41_out, INSTRUCTION[6]);
  and and_29 (and_29_out, Opcode13_14, INSTRUCTION[6], T4, INSTRUCTION[10]);
  and and_30 (and_30_out, Opcode13_14, INSTRUCTION[6], T6, INSTRUCTION[10]);
  or or_19 (or_19_out, INSTRUCTION[2], INSTRUCTION[6]);
  and and_31 (and_31_out, Opcode6_9_10, INSTRUCTION[6], INSTRUCTION[10], T4);
  and and_32 (and_32_out, Opcode6_9_10, not_41_out, INSTRUCTION[10], T5);
  and and_33 (and_33_out, Opcode4_5_7_8, T4, INSTRUCTION[2], INSTRUCTION[10], INSTRUCTION[6]);
  and and_34 (and_34_out, Opcode4_5_7_8, T5, or_19_out, INSTRUCTION[10]);
  and and_35 (and_35_out, Opcode4_5_7_8, T6, not_39_out, INSTRUCTION[10], not_40_out);
  and and_36 (and_36_out, T4, INSTRUCTION[6], INSTRUCTION[10], Opcode3);
  not not_42 (not_42_out, INSTRUCTION[10]);
  and and_37 (and_37_out, T4, not_42_out, Opcode1);
  and and_38 (and_38_out, T5, Opcode11);
  or or_20 (or_20_out, and_37_out, and_38_out);
  or or_21 (or_21_out, and_28_out, and_27_out, and_26_out, and_25_out, and_24_out, and_23_out, and_22_out, and_21_out, and_17_out, and_18_out, and_19_out, and_20_out);
  or or_22 (or_22_out, and_15_out, and_35_out, and_34_out, and_36_out, and_33_out, and_30_out, and_29_out, and_32_out, and_31_out, and_16_out);
  assign MuxASel = or_20_out ? 2'b01 : 2'bz;  // Controlled_Buffer controlled_buffer_6
  and and_39 (and_39_out, T4, INSTRUCTION[10], Opcode1);
  assign MuxASel = and_39_out ? 2'b10 : 2'bz;  // Controlled_Buffer controlled_buffer_7
  assign MuxASel = or_21_out ? 2'b11 : 2'bz;  // Controlled_Buffer controlled_buffer_8
  assign MuxASel = or_22_out ? 2'b00 : 2'bz;  // Controlled_Buffer controlled_buffer_9
  or or_23 (or_23_out, INSTRUCTION[3], INSTRUCTION[6]);
  not not_43 (not_43_out, Z);
  not not_44 (not_44_out, INSTRUCTION[6]);
  not not_45 (not_45_out, INSTRUCTION[10]);
  not not_46 (not_46_out, INSTRUCTION[10]);
  not not_47 (not_47_out, INSTRUCTION[10]);
  not not_48 (not_48_out, INSTRUCTION[3]);
  not not_49 (not_49_out, INSTRUCTION[6]);
  not not_50 (not_50_out, INSTRUCTION[10]);
  not not_51 (not_51_out, INSTRUCTION[10]);
  not not_52 (not_52_out, INSTRUCTION[6]);
  not not_53 (not_53_out, INSTRUCTION[10]);
  not not_54 (not_54_out, INSTRUCTION[10]);
  not not_55 (not_55_out, INSTRUCTION[10]);
  not not_56 (not_56_out, INSTRUCTION[6]);
  not not_57 (not_57_out, INSTRUCTION[10]);
  and and_40 (and_40_out, Opcode4, not_44_out, not_45_out, T4);
  and and_41 (and_41_out, Opcode3, INSTRUCTION[6], not_46_out, T4);
  and and_42 (and_42_out, Opcode4_5_7_8, INSTRUCTION[3], INSTRUCTION[6], not_47_out, T4);
  and and_43 (and_43_out, Opcode4_5_7_8, not_48_out, not_49_out, not_50_out, T6);
  and and_44 (and_44_out, Opcode4_5_7_8, or_23_out, not_51_out, T5);
  and and_45 (and_45_out, Opcode6_9_10, not_52_out, T5, not_53_out);
  and and_46 (and_46_out, Opcode6_9_10, INSTRUCTION[6], T5, not_54_out);
  and and_47 (and_47_out, Opcode13_14, INSTRUCTION[6], not_55_out, T6);
  and and_48 (and_48_out, Opcode13_14, not_56_out, not_57_out, T6);
  and and_49 (and_49_out, Opcode0, T4);
  and and_50 (and_50_out, Opcode15, not_43_out, T4);
  or or_24 (or_24_out, and_49_out, and_50_out);
  or or_25 (or_25_out, and_41_out, and_42_out, and_43_out, and_44_out, and_45_out, and_46_out, and_47_out, and_48_out);
  assign MuxBSel = 1'b0 ? 2'b01 : 2'bz;  // Controlled_Buffer controlled_buffer_10
  assign MuxBSel = or_24_out ? 2'b10 : 2'bz;  // Controlled_Buffer controlled_buffer_11
  assign MuxBSel = and_40_out ? 2'b11 : 2'bz;  // Controlled_Buffer controlled_buffer_12
  assign MuxBSel = or_25_out ? 2'b00 : 2'bz;  // Controlled_Buffer controlled_buffer_13
  not not_58 (not_58_out, INSTRUCTION[2]);
  not not_59 (not_59_out, INSTRUCTION[2]);
  not not_60 (not_60_out, INSTRUCTION[2]);
  not not_61 (not_61_out, INSTRUCTION[10]);
  not not_62 (not_62_out, INSTRUCTION[6]);
  not not_63 (not_63_out, INSTRUCTION[10]);
  not not_64 (not_64_out, INSTRUCTION[2]);
  not not_65 (not_65_out, INSTRUCTION[6]);
  not not_66 (not_66_out, INSTRUCTION[2]);
  not not_67 (not_67_out, INSTRUCTION[2]);
  not not_68 (not_68_out, INSTRUCTION[6]);
  not not_69 (not_69_out, INSTRUCTION[10]);
  not not_70 (not_70_out, INSTRUCTION[10]);
  not not_71 (not_71_out, INSTRUCTION[6]);
  not not_72 (not_72_out, INSTRUCTION[10]);
  not not_73 (not_73_out, INSTRUCTION[6]);
  not not_74 (not_74_out, INSTRUCTION[6]);
  not not_75 (not_75_out, INSTRUCTION[10]);
  and and_51 (and_51_out, T6, INSTRUCTION[10], not_67_out, not_68_out, Opcode4);
  and and_52 (and_52_out, T4, not_69_out, INSTRUCTION[2], INSTRUCTION[6], Opcode4);
  and and_53 (and_53_out, T5, not_70_out, INSTRUCTION[2], not_71_out, Opcode4);
  and and_54 (and_54_out, T5, not_72_out, not_58_out, INSTRUCTION[6], Opcode4);
  and and_55 (and_55_out, T5, INSTRUCTION[10], INSTRUCTION[2], not_73_out, Opcode4);
  and and_56 (and_56_out, T5, INSTRUCTION[10], not_59_out, INSTRUCTION[6], Opcode4);
  and and_57 (and_57_out, T6, INSTRUCTION[10], not_60_out, not_74_out, Opcode5);
  and and_58 (and_58_out, T4, INSTRUCTION[10], INSTRUCTION[2], INSTRUCTION[6], Opcode5);
  and and_59 (and_59_out, T4, not_75_out, INSTRUCTION[2], INSTRUCTION[6], Opcode5);
  and and_60 (and_60_out, T5, not_61_out, INSTRUCTION[2], not_62_out, Opcode5);
  and and_61 (and_61_out, T5, not_63_out, not_64_out, INSTRUCTION[6], Opcode5);
  and and_62 (and_62_out, T5, INSTRUCTION[10], INSTRUCTION[2], not_65_out, Opcode5);
  and and_63 (and_63_out, T5, INSTRUCTION[10], not_66_out, INSTRUCTION[6], Opcode5);
  and and_64 (and_64_out, T4, INSTRUCTION[10], INSTRUCTION[2], INSTRUCTION[6], Opcode4);
  not not_76 (not_76_out, INSTRUCTION[2]);
  not not_77 (not_77_out, INSTRUCTION[10]);
  not not_78 (not_78_out, INSTRUCTION[2]);
  not not_79 (not_79_out, INSTRUCTION[6]);
  not not_80 (not_80_out, INSTRUCTION[10]);
  not not_81 (not_81_out, INSTRUCTION[6]);
  or or_26 (Opcode13_14, Opcode13, Opcode14);
  and and_65 (and_65_out, T6, not_77_out, not_78_out, not_79_out, Opcode4);
  and and_66 (and_66_out, T6, not_80_out, not_76_out, not_81_out, Opcode5);
  or or_27 (or_27_out, and_51_out, and_64_out, and_52_out, and_53_out, and_54_out, and_55_out, and_56_out, and_65_out);
  or or_28 (or_28_out, and_57_out, and_58_out, and_59_out, and_60_out, and_61_out, and_62_out, and_63_out, and_66_out);
  or or_29 (or_29_out, T4, T6);
  not not_82 (not_82_out, INSTRUCTION[2]);
  not not_83 (not_83_out, INSTRUCTION[6]);
  not not_84 (not_84_out, INSTRUCTION[2]);
  not not_85 (not_85_out, INSTRUCTION[10]);
  not not_86 (not_86_out, INSTRUCTION[6]);
  or or_30 (or_30_out, T4, T6);
  not not_87 (not_87_out, INSTRUCTION[2]);
  not not_88 (not_88_out, INSTRUCTION[6]);
  not not_89 (not_89_out, INSTRUCTION[2]);
  not not_90 (not_90_out, INSTRUCTION[6]);
  not not_91 (not_91_out, INSTRUCTION[2]);
  not not_92 (not_92_out, INSTRUCTION[2]);
  not not_93 (not_93_out, INSTRUCTION[6]);
  not not_94 (not_94_out, INSTRUCTION[10]);
  not not_95 (not_95_out, INSTRUCTION[10]);
  not not_96 (not_96_out, INSTRUCTION[6]);
  not not_97 (not_97_out, INSTRUCTION[10]);
  and and_67 (and_67_out, T6, not_85_out, not_86_out, Opcode13_14);
  not not_98 (not_98_out, INSTRUCTION[6]);
  not not_99 (not_99_out, INSTRUCTION[10]);
  not not_100 (not_100_out, INSTRUCTION[6]);
  not not_101 (not_101_out, INSTRUCTION[10]);
  not not_102 (not_102_out, INSTRUCTION[10]);
  not not_103 (not_103_out, INSTRUCTION[10]);
  and and_68 (and_68_out, T6, INSTRUCTION[10], not_98_out, Opcode13_14);
  and and_69 (and_69_out, or_29_out, not_99_out, INSTRUCTION[6], Opcode13_14);
  and and_70 (and_70_out, or_30_out, INSTRUCTION[10], INSTRUCTION[6], Opcode13_14);
  not not_104 (not_104_out, INSTRUCTION[10]);
  not not_105 (not_105_out, INSTRUCTION[10]);
  not not_106 (not_106_out, INSTRUCTION[6]);
  not not_107 (not_107_out, INSTRUCTION[6]);
  not not_108 (not_108_out, INSTRUCTION[10]);
  not not_109 (not_109_out, INSTRUCTION[10]);
  not not_110 (not_110_out, INSTRUCTION[6]);
  not not_111 (not_111_out, INSTRUCTION[6]);
  and and_71 (and_71_out, T6, INSTRUCTION[10], not_92_out, not_93_out, Opcode8);
  and and_72 (and_72_out, T4, INSTRUCTION[10], INSTRUCTION[2], INSTRUCTION[6], Opcode8);
  and and_73 (and_73_out, T4, not_94_out, INSTRUCTION[2], INSTRUCTION[6], Opcode8);
  and and_74 (and_74_out, T5, not_95_out, INSTRUCTION[2], not_96_out, Opcode8);
  and and_75 (and_75_out, T5, not_97_out, not_82_out, INSTRUCTION[6], Opcode8);
  and and_76 (and_76_out, T5, INSTRUCTION[10], INSTRUCTION[2], not_83_out, Opcode8);
  and and_77 (and_77_out, T5, INSTRUCTION[10], not_84_out, INSTRUCTION[6], Opcode8);
  and and_78 (and_78_out, T6, INSTRUCTION[10], not_87_out, not_100_out, Opcode7);
  and and_79 (and_79_out, T4, INSTRUCTION[10], INSTRUCTION[2], INSTRUCTION[6], Opcode7);
  and and_80 (and_80_out, T4, not_101_out, INSTRUCTION[2], INSTRUCTION[6], Opcode7);
  and and_81 (and_81_out, T5, not_102_out, INSTRUCTION[2], not_88_out, Opcode7);
  and and_82 (and_82_out, T5, not_103_out, not_89_out, INSTRUCTION[6], Opcode7);
  and and_83 (and_83_out, T5, INSTRUCTION[10], INSTRUCTION[2], not_90_out, Opcode7);
  and and_84 (and_84_out, T5, INSTRUCTION[10], not_91_out, INSTRUCTION[6], Opcode7);
  and and_85 (and_85_out, Opcode3, INSTRUCTION[6], T4);
  not not_112 (not_112_out, INSTRUCTION[10]);
  not not_113 (not_113_out, INSTRUCTION[6]);
  not not_114 (not_114_out, INSTRUCTION[10]);
  not not_115 (not_115_out, INSTRUCTION[6]);
  and and_86 (and_86_out, T4, not_104_out, INSTRUCTION[6], Opcode9);
  and and_87 (and_87_out, T5, not_105_out, not_106_out, Opcode9);
  and and_88 (and_88_out, T5, INSTRUCTION[10], not_107_out, Opcode9);
  and and_89 (and_89_out, T5, not_109_out, not_110_out, Opcode10);
  and and_90 (and_90_out, T5, INSTRUCTION[10], not_111_out, Opcode10);
  and and_91 (and_91_out, Opcode12, T4);
  and and_92 (and_92_out, T4, INSTRUCTION[10], INSTRUCTION[6], Opcode6);
  and and_93 (and_93_out, T4, not_112_out, INSTRUCTION[6], Opcode6);
  and and_94 (and_94_out, T5, INSTRUCTION[10], not_113_out, Opcode6);
  and and_95 (and_95_out, T5, not_114_out, not_115_out, Opcode6);
  and and_96 (and_96_out, T4, INSTRUCTION[10], INSTRUCTION[6], Opcode9);
  and and_97 (and_97_out, T4, INSTRUCTION[10], INSTRUCTION[6], Opcode10);
  and and_98 (and_98_out, T4, not_108_out, INSTRUCTION[6], Opcode10);
  not not_116 (not_116_out, INSTRUCTION[10]);
  not not_117 (not_117_out, INSTRUCTION[2]);
  not not_118 (not_118_out, INSTRUCTION[6]);
  and and_99 (and_99_out, Opcode2, T4);
  not not_119 (not_119_out, INSTRUCTION[10]);
  not not_120 (not_120_out, INSTRUCTION[2]);
  not not_121 (not_121_out, INSTRUCTION[6]);
  and and_100 (and_100_out, T6, not_116_out, not_117_out, not_118_out, Opcode8);
  or or_31 (or_31_out, and_92_out, and_93_out, and_94_out, and_95_out);
  and and_101 (and_101_out, T6, not_119_out, not_120_out, not_121_out, Opcode7);
  or or_32 (or_32_out, and_71_out, and_72_out, and_73_out, and_74_out, and_75_out, and_76_out, and_77_out, and_100_out);
  or or_33 (or_33_out, and_85_out, and_91_out, and_68_out, and_99_out, and_67_out, and_69_out, and_70_out);
  assign FunSel_ALU = or_33_out ? 4'b0000 : 4'bz;  // Controlled_Buffer controlled_buffer_14
  assign FunSel_ALU = or_31_out ? 4'b0010 : 4'bz;  // Controlled_Buffer controlled_buffer_15
  assign FunSel_ALU = or_27_out ? 4'b0111 : 4'bz;  // Controlled_Buffer controlled_buffer_16
  assign FunSel_ALU = or_28_out ? 4'b1000 : 4'bz;  // Controlled_Buffer controlled_buffer_17
  or or_34 (or_34_out, and_96_out, and_86_out, and_87_out, and_88_out);
  or or_35 (or_35_out, and_97_out, and_98_out, and_89_out, and_90_out);
  or or_36 (or_36_out, and_78_out, and_79_out, and_80_out, and_81_out, and_82_out, and_83_out, and_84_out, and_101_out);
  assign FunSel_ALU = or_32_out ? 4'b0110 : 4'bz;  // Controlled_Buffer controlled_buffer_18
  assign FunSel_ALU = or_34_out ? 4'b1010 : 4'bz;  // Controlled_Buffer controlled_buffer_19
  assign FunSel_ALU = or_35_out ? 4'b1011 : 4'bz;  // Controlled_Buffer controlled_buffer_20
  assign FunSel_ALU = or_36_out ? 4'b0100 : 4'bz;  // Controlled_Buffer controlled_buffer_21
  not not_122 (not_122_out, INSTRUCTION[2]);
  not not_123 (not_123_out, INSTRUCTION[6]);
  not not_124 (not_124_out, INSTRUCTION[2]);
  not not_125 (not_125_out, INSTRUCTION[6]);
  not not_126 (not_126_out, INSTRUCTION[10]);
  not not_127 (not_127_out, INSTRUCTION[10]);
  not not_128 (not_128_out, INSTRUCTION[6]);
  not not_129 (not_129_out, INSTRUCTION[10]);
  not not_130 (not_130_out, INSTRUCTION[6]);
  and and_102 (and_102_out, INSTRUCTION[6], INSTRUCTION[10]);
  and and_103 (and_103_out, INSTRUCTION[6], not_131_out);
  not not_131 (not_131_out, INSTRUCTION[10]);
  and and_104 (and_104_out, not_122_out, not_123_out, INSTRUCTION[10]);
  and and_105 (and_105_out, not_124_out, not_125_out, not_126_out);
  and and_106 (and_106_out, INSTRUCTION[2], INSTRUCTION[6], INSTRUCTION[10]);
  and and_107 (and_107_out, INSTRUCTION[2], INSTRUCTION[6], not_127_out);
  and and_108 (and_108_out, INSTRUCTION[2], not_128_out, not_129_out);
  and and_109 (and_109_out, INSTRUCTION[2], not_130_out, INSTRUCTION[10]);
  or or_37 (or_37_out, Opcode3, Opcode6_9_10, Opcode13_14);
  or or_38 (or_38_out, Opcode3, Opcode6_9_10, Opcode13_14);
  and and_110 (and_110_out, T4, and_102_out, or_37_out);
  and and_111 (and_111_out, T4, and_103_out, or_38_out);
  and and_112 (and_112_out, T4, Opcode2);
  and and_113 (and_113_out, T6, and_104_out, Opcode4_5_7_8);
  and and_114 (and_114_out, T6, and_105_out, Opcode4_5_7_8);
  and and_115 (and_115_out, T6, Opcode13_14);
  and and_116 (and_116_out, T4, and_106_out, Opcode4_5_7_8);
  and and_117 (and_117_out, T4, and_107_out, Opcode4_5_7_8);
  and and_118 (and_118_out, T5, and_108_out, Opcode4_5_7_8);
  and and_119 (and_119_out, T5, and_109_out, Opcode4_5_7_8);
  or or_39 (or_39_out, and_110_out, and_111_out);
  or or_40 (or_40_out, and_113_out, and_114_out, and_115_out);
  or or_41 (or_41_out, and_116_out, and_117_out, and_118_out, and_119_out);
  assign OutASel = and_112_out ? {1'b0, INSTRUCTION[9:8]} : 3'bz;  // Controlled_Buffer controlled_buffer_22
  assign OutASel = or_40_out ? 3'b100 : 3'bz;  // Controlled_Buffer controlled_buffer_23
  assign OutASel = or_41_out ? {1'b0, INSTRUCTION[1:0]} : 3'bz;  // Controlled_Buffer controlled_buffer_24
  assign OutASel = or_39_out ? {1'b0, INSTRUCTION[5:4]} : 3'bz;  // Controlled_Buffer controlled_buffer_25
  not not_132 (not_132_out, INSTRUCTION[2]);
  not not_133 (not_133_out, INSTRUCTION[6]);
  not not_134 (not_134_out, INSTRUCTION[2]);
  not not_135 (not_135_out, INSTRUCTION[6]);
  not not_136 (not_136_out, INSTRUCTION[10]);
  and and_120 (and_120_out, INSTRUCTION[2], INSTRUCTION[6], INSTRUCTION[10]);
  and and_121 (and_121_out, INSTRUCTION[2], INSTRUCTION[6], not_137_out);
  not not_137 (not_137_out, INSTRUCTION[10]);
  and and_122 (and_122_out, INSTRUCTION[2], not_138_out, not_139_out);
  not not_138 (not_138_out, INSTRUCTION[6]);
  not not_139 (not_139_out, INSTRUCTION[10]);
  not not_140 (not_140_out, INSTRUCTION[2]);
  and and_123 (and_123_out, not_140_out, INSTRUCTION[6], not_141_out);
  not not_141 (not_141_out, INSTRUCTION[10]);
  not not_142 (not_142_out, INSTRUCTION[6]);
  and and_124 (and_124_out, INSTRUCTION[2], not_142_out, INSTRUCTION[10]);
  not not_143 (not_143_out, INSTRUCTION[2]);
  and and_125 (and_125_out, not_143_out, INSTRUCTION[6], INSTRUCTION[10]);
  and and_126 (and_126_out, not_132_out, not_133_out, INSTRUCTION[10]);
  and and_127 (and_127_out, not_134_out, not_135_out, not_136_out);
  and and_128 (and_128_out, T4, and_120_out, Opcode4_5_7_8);
  and and_129 (and_129_out, T4, and_121_out, Opcode4_5_7_8);
  and and_130 (and_130_out, T5, and_122_out, Opcode4_5_7_8);
  and and_131 (and_131_out, T5, and_123_out, Opcode4_5_7_8);
  and and_132 (and_132_out, T5, and_124_out, Opcode4_5_7_8);
  and and_133 (and_133_out, T5, and_125_out, Opcode4_5_7_8);
  and and_134 (and_134_out, T6, and_126_out, Opcode4_5_7_8);
  and and_135 (and_135_out, T6, and_127_out, Opcode4_5_7_8);
  or or_42 (or_42_out, and_134_out, and_135_out);
  or or_43 (or_43_out, and_128_out, and_129_out);
  or or_44 (or_44_out, and_130_out, and_131_out, and_132_out, and_133_out);
  assign OutBSel = or_43_out ? {1'b0, INSTRUCTION[5:4]} : 3'bz;  // Controlled_Buffer controlled_buffer_26
  assign OutBSel = or_44_out ? 3'b100 : 3'bz;  // Controlled_Buffer controlled_buffer_27
  assign OutBSel = or_42_out ? 3'b101 : 3'bz;  // Controlled_Buffer controlled_buffer_28
  not not_144 (not_144_out, INSTRUCTION[6]);
  not not_145 (not_145_out, INSTRUCTION[2]);
  not not_146 (not_146_out, INSTRUCTION[2]);
  not not_147 (not_147_out, INSTRUCTION[6]);
  and and_136 (and_136_out, INSTRUCTION[6], INSTRUCTION[10]);
  and and_137 (and_137_out, INSTRUCTION[10], not_148_out);
  not not_148 (not_148_out, INSTRUCTION[6]);
  and and_138 (and_138_out, INSTRUCTION[10], not_149_out);
  not not_149 (not_149_out, INSTRUCTION[6]);
  and and_139 (and_139_out, INSTRUCTION[2], INSTRUCTION[6], INSTRUCTION[10]);
  and and_140 (and_140_out, INSTRUCTION[2], not_144_out, INSTRUCTION[10]);
  and and_141 (and_141_out, not_145_out, INSTRUCTION[6], INSTRUCTION[10]);
  and and_142 (and_142_out, not_146_out, not_147_out, INSTRUCTION[10]);
  or or_45 (or_45_out, Opcode3, Opcode6_9_10);
  and and_143 (and_143_out, T4, and_136_out, or_45_out);
  and and_144 (and_144_out, T4, and_137_out, Opcode3);
  and and_145 (and_145_out, T5, and_138_out, Opcode6_9_10);
  and and_146 (and_146_out, T5, Opcode11);
  and and_147 (and_147_out, T4, Opcode1);
  and and_148 (and_148_out, T4, and_139_out, Opcode4_5_7_8);
  and and_149 (and_149_out, T5, and_140_out, Opcode4_5_7_8);
  and and_150 (and_150_out, T5, and_141_out, Opcode4_5_7_8);
  and and_151 (and_151_out, T6, and_142_out, Opcode4_5_7_8);
  and and_152 (and_152_out, Opcode13_14, T6, INSTRUCTION[10]);
  or or_46 (or_46_out, and_148_out, and_149_out, and_150_out, and_151_out, and_143_out, and_144_out, and_145_out, and_152_out);
  assign RegSelRF = or_46_out ? DESTREGRF : 4'bz;  // Controlled_Buffer controlled_buffer_29
  or or_47 (or_47_out, and_146_out, and_147_out);
  assign RegSelRF = or_47_out ? RegSelRF_t : 4'bz;  // Controlled_Buffer controlled_buffer_30
  not not_150 (not_150_out, INSTRUCTION[6]);
  not not_151 (not_151_out, INSTRUCTION[10]);
  not not_152 (not_152_out, INSTRUCTION[2]);
  not not_153 (not_153_out, INSTRUCTION[10]);
  not not_154 (not_154_out, INSTRUCTION[6]);
  not not_155 (not_155_out, INSTRUCTION[2]);
  not not_156 (not_156_out, INSTRUCTION[2]);
  not not_157 (not_157_out, INSTRUCTION[6]);
  not not_158 (not_158_out, INSTRUCTION[2]);
  not not_159 (not_159_out, INSTRUCTION[6]);
  not not_160 (not_160_out, INSTRUCTION[10]);
  and and_153 (and_153_out, INSTRUCTION[2], not_150_out, not_151_out);
  and and_154 (and_154_out, not_152_out, INSTRUCTION[6], not_153_out);
  and and_155 (and_155_out, INSTRUCTION[2], not_154_out, INSTRUCTION[10]);
  and and_156 (and_156_out, not_155_out, INSTRUCTION[6], INSTRUCTION[10]);
  and and_157 (and_157_out, not_156_out, not_157_out, INSTRUCTION[10]);
  and and_158 (and_158_out, not_158_out, not_159_out, not_160_out);
  and and_159 (and_159_out, INSTRUCTION[10], not_161_out);
  not not_161 (not_161_out, INSTRUCTION[6]);
  not not_162 (not_162_out, INSTRUCTION[10]);
  and and_160 (and_160_out, not_162_out, not_163_out);
  not not_163 (not_163_out, INSTRUCTION[6]);
  or or_48 (or_48_out, T4, T5);
  or or_49 (or_49_out, Opcode14, Opcode13);
  and and_161 (and_161_out, T4, and_153_out, Opcode4_5_7_8);
  and and_162 (and_162_out, T4, and_154_out, Opcode4_5_7_8);
  and and_163 (and_163_out, T4, and_155_out, Opcode4_5_7_8);
  and and_164 (and_164_out, T4, and_156_out, Opcode4_5_7_8);
  and and_165 (and_165_out, or_48_out, or_49_out);
  and and_166 (and_166_out, T5, and_157_out, Opcode4_5_7_8);
  and and_167 (and_167_out, T5, and_158_out, Opcode4_5_7_8);
  and and_168 (and_168_out, T4, and_159_out, Opcode6_9_10);
  and and_169 (and_169_out, T4, and_160_out, Opcode6_9_10);
  or or_50 (or_50_out, and_166_out, and_167_out);
  or or_51 (or_51_out, and_168_out, and_169_out);
  or or_52 (or_52_out, and_161_out, and_162_out, and_163_out, and_164_out, and_165_out);
  assign TempSel = or_50_out ? 4'b1011 : 4'bz;  // Controlled_Buffer controlled_buffer_31
  assign TempSel = or_51_out ? 4'b1110 : 4'bz;  // Controlled_Buffer controlled_buffer_32
  assign TempSel = or_52_out ? 4'b0111 : 4'bz;  // Controlled_Buffer controlled_buffer_33
  not not_164 (not_164_out, INSTRUCTION[6]);
  not not_165 (not_165_out, INSTRUCTION[6]);
  not not_166 (not_166_out, INSTRUCTION[10]);
  not not_167 (not_167_out, INSTRUCTION[6]);
  not not_168 (not_168_out, INSTRUCTION[10]);
  not not_169 (not_169_out, INSTRUCTION[6]);
  not not_170 (not_170_out, INSTRUCTION[2]);
  not not_171 (not_171_out, INSTRUCTION[6]);
  not not_172 (not_172_out, INSTRUCTION[2]);
  not not_173 (not_173_out, INSTRUCTION[6]);
  not not_174 (not_174_out, INSTRUCTION[10]);
  not not_175 (not_175_out, INSTRUCTION[2]);
  not not_176 (not_176_out, INSTRUCTION[10]);
  not not_177 (not_177_out, INSTRUCTION[2]);
  not not_178 (not_178_out, INSTRUCTION[2]);
  not not_179 (not_179_out, INSTRUCTION[6]);
  not not_180 (not_180_out, INSTRUCTION[2]);
  not not_181 (not_181_out, INSTRUCTION[6]);
  not not_182 (not_182_out, INSTRUCTION[10]);
  and and_170 (and_170_out, Opcode3_6_9_10_13_14, not_164_out, INSTRUCTION[10], T4);
  and and_171 (and_171_out, Opcode3_6_9_10_13_14, not_165_out, not_166_out, T4);
  and and_172 (and_172_out, Opcode4_5_7_8, INSTRUCTION[2], not_167_out, not_168_out, T4);
  and and_173 (and_173_out, Opcode4_5_7_8, INSTRUCTION[2], not_169_out, INSTRUCTION[10], T4);
  and and_174 (and_174_out, Opcode4_5_7_8, not_170_out, not_171_out, INSTRUCTION[10], T5);
  and and_175 (and_175_out, Opcode4_5_7_8, not_172_out, not_173_out, not_174_out, T5);
  and and_176 (and_176_out, Opcode4_5_7_8, not_175_out, INSTRUCTION[6], not_176_out, T4);
  and and_177 (and_177_out, Opcode4_5_7_8, not_177_out, INSTRUCTION[6], INSTRUCTION[10], T4);
  and and_178 (and_178_out, Opcode4_5_7_8, not_178_out, not_179_out, INSTRUCTION[10], T4);
  and and_179 (and_179_out, Opcode4_5_7_8, not_180_out, not_181_out, not_182_out, T4);
  or or_53 (or_53_out, and_170_out, and_171_out, and_172_out, and_173_out, and_174_out, and_175_out);
  assign OutCSel = or_53_out ? INSTRUCTION[5:4] : 2'bz;  // Controlled_Buffer controlled_buffer_34
  or or_54 (or_54_out, and_176_out, and_177_out, and_178_out, and_179_out);
  assign OutCSel = or_54_out ? INSTRUCTION[1:0] : 2'bz;  // Controlled_Buffer controlled_buffer_35
  not not_183 (not_183_out, INSTRUCTION[10]);
  not not_184 (not_184_out, INSTRUCTION[6]);
  not not_185 (not_185_out, INSTRUCTION[10]);
  not not_186 (not_186_out, INSTRUCTION[6]);
  not not_187 (not_187_out, INSTRUCTION[10]);
  not not_188 (not_188_out, INSTRUCTION[2]);
  not not_189 (not_189_out, INSTRUCTION[10]);
  not not_190 (not_190_out, INSTRUCTION[2]);
  not not_191 (not_191_out, INSTRUCTION[6]);
  not not_192 (not_192_out, INSTRUCTION[10]);
  not not_193 (not_193_out, INSTRUCTION[10]);
  not not_194 (not_194_out, INSTRUCTION[6]);
  not not_195 (not_195_out, INSTRUCTION[10]);
  not not_196 (not_196_out, INSTRUCTION[10]);
  not not_197 (not_197_out, INSTRUCTION[6]);
  not not_198 (not_198_out, INSTRUCTION[10]);
  not not_199 (not_199_out, Z);
  and and_180 (and_180_out, Opcode4_5_7_8, INSTRUCTION[2], INSTRUCTION[6], not_183_out, T4);
  and and_181 (and_181_out, Opcode4_5, INSTRUCTION[2], not_184_out, not_185_out, T4);
  and and_182 (and_182_out, Opcode7_8, INSTRUCTION[2], not_186_out, not_187_out, T5);
  and and_183 (and_183_out, Opcode4_5_7_8, not_188_out, INSTRUCTION[6], not_189_out, T5);
  and and_184 (and_184_out, Opcode4_5_7_8, not_190_out, not_191_out, not_192_out, T6);
  and and_185 (and_185_out, Opcode3_6_9_10, INSTRUCTION[6], not_193_out, T4);
  and and_186 (and_186_out, Opcode3_6_9_10, not_194_out, not_195_out, T5);
  and and_187 (and_187_out, Opcode13_14, INSTRUCTION[6], not_196_out, T6);
  and and_188 (and_188_out, Opcode13_14, not_197_out, not_198_out, T6);
  and and_189 (and_189_out, Opcode0, T4);
  and and_190 (and_190_out, Opcode15, not_199_out, T4);
  and and_191 (and_191_out, Opcode11_12, T4);
  or or_55 (or_55_out, and_180_out, and_181_out, and_182_out, and_183_out, and_184_out, and_185_out, and_186_out, and_187_out, and_188_out);
  or or_56 (or_56_out, T1, T3, and_189_out, and_190_out);
  assign RegSelARF = or_56_out ? 3'b011 : 3'bz;  // Controlled_Buffer controlled_buffer_36
  assign RegSelARF = and_191_out ? 3'b110 : 3'bz;  // Controlled_Buffer controlled_buffer_37
  assign RegSelARF = or_55_out ? DESTREGARF : 3'bz;  // Controlled_Buffer controlled_buffer_38
  not not_200 (not_200_out, INSTRUCTION[6]);
  not not_201 (not_201_out, INSTRUCTION[10]);
  not not_202 (not_202_out, INSTRUCTION[2]);
  not not_203 (not_203_out, INSTRUCTION[10]);
  not not_204 (not_204_out, INSTRUCTION[6]);
  not not_205 (not_205_out, INSTRUCTION[2]);
  not not_206 (not_206_out, INSTRUCTION[2]);
  not not_207 (not_207_out, INSTRUCTION[6]);
  not not_208 (not_208_out, INSTRUCTION[2]);
  not not_209 (not_209_out, INSTRUCTION[6]);
  not not_210 (not_210_out, INSTRUCTION[10]);
  and and_192 (and_192_out, INSTRUCTION[6], INSTRUCTION[10]);
  not not_211 (not_211_out, INSTRUCTION[6]);
  not not_212 (not_212_out, INSTRUCTION[6]);
  not not_213 (not_213_out, INSTRUCTION[6]);
  not not_214 (not_214_out, INSTRUCTION[10]);
  and and_193 (and_193_out, INSTRUCTION[2], INSTRUCTION[6], INSTRUCTION[10]);
  and and_194 (and_194_out, INSTRUCTION[2], not_200_out, not_201_out);
  and and_195 (and_195_out, not_202_out, INSTRUCTION[6], not_203_out);
  and and_196 (and_196_out, INSTRUCTION[2], not_204_out, INSTRUCTION[10]);
  and and_197 (and_197_out, not_205_out, INSTRUCTION[6], INSTRUCTION[10]);
  and and_198 (and_198_out, not_206_out, not_207_out, INSTRUCTION[10]);
  and and_199 (and_199_out, not_208_out, not_209_out, not_210_out);
  not not_215 (not_215_out, INSTRUCTION[10]);
  and and_200 (and_200_out, not_211_out, INSTRUCTION[10]);
  and and_201 (and_201_out, not_212_out, INSTRUCTION[10]);
  and and_202 (and_202_out, not_213_out, not_214_out);
  or or_57 (or_57_out, T4, T5);
  or or_58 (or_58_out, T4, T5);
  or or_59 (or_59_out, T4, T5, T6);
  or or_60 (or_60_out, T4, T5);
  and and_203 (and_203_out, INSTRUCTION[6], not_215_out);
  or or_61 (or_61_out, Opcode13_14, Opcode3, Opcode6_9_10);
  or or_62 (or_62_out, Opcode3, Opcode6_9_10, Opcode13_14);
  or or_63 (or_63_out, Opcode13_14, Opcode6_9_10);
  and and_204 (and_204_out, INSTRUCTION[10], T6, Opcode13_14);
  and and_205 (and_205_out, T4, Opcode1);
  and and_206 (and_206_out, T4, and_192_out, or_61_out);
  and and_207 (and_207_out, T4, and_200_out, or_62_out);
  and and_208 (and_208_out, T5, and_201_out, Opcode6_9_10);
  and and_209 (and_209_out, T4, and_202_out, or_63_out);
  and and_210 (and_210_out, T4, and_193_out, Opcode4_5_7_8);
  and and_211 (and_211_out, T4, and_194_out, Opcode4_5_7_8);
  and and_212 (and_212_out, T4, and_195_out, Opcode4_5_7_8);
  and and_213 (and_213_out, or_57_out, and_196_out, Opcode4_5_7_8);
  and and_214 (and_214_out, or_58_out, and_197_out, Opcode4_5_7_8);
  and and_215 (and_215_out, or_59_out, and_198_out, Opcode4_5_7_8);
  and and_216 (and_216_out, or_60_out, and_199_out, Opcode4_5_7_8);
  and and_217 (and_217_out, T5, Opcode11);
  and and_218 (and_218_out, T4, and_203_out, Opcode13_14);
  and and_219 (and_219_out, T5, Opcode14);
  and and_220 (and_220_out, T5, Opcode13);
  or or_64 (or_64_out, and_204_out, and_205_out, and_206_out, and_207_out, and_208_out, and_209_out, and_210_out, and_211_out, and_212_out, and_213_out, and_214_out, and_215_out, and_216_out, and_217_out, and_218_out);
  assign FunSel_RF = and_220_out ? 2'b01 : 2'bz;  // Controlled_Buffer controlled_buffer_39
  assign FunSel_RF = and_219_out ? 2'b00 : 2'bz;  // Controlled_Buffer controlled_buffer_40
  assign FunSel_RF = or_64_out ? 2'b10 : 2'bz;  // Controlled_Buffer controlled_buffer_41
  not not_216 (not_216_out, INSTRUCTION[6]);
  not not_217 (not_217_out, INSTRUCTION[6]);
  not not_218 (not_218_out, INSTRUCTION[6]);
  not not_219 (not_219_out, INSTRUCTION[10]);
  not not_220 (not_220_out, INSTRUCTION[2]);
  not not_221 (not_221_out, INSTRUCTION[10]);
  not not_222 (not_222_out, INSTRUCTION[2]);
  not not_223 (not_223_out, INSTRUCTION[6]);
  not not_224 (not_224_out, INSTRUCTION[10]);
  not not_225 (not_225_out, INSTRUCTION[6]);
  not not_226 (not_226_out, INSTRUCTION[10]);
  not not_227 (not_227_out, INSTRUCTION[10]);
  not not_228 (not_228_out, INSTRUCTION[10]);
  not not_229 (not_229_out, INSTRUCTION[10]);
  not not_230 (not_230_out, INSTRUCTION[10]);
  not not_231 (not_231_out, Z);
  and and_221 (and_221_out, Opcode11, T4);
  and and_222 (and_222_out, Opcode0, T4);
  and and_223 (and_223_out, Opcode3_6_9_10, INSTRUCTION[6], not_226_out, T4);
  and and_224 (and_224_out, Opcode3, not_216_out, not_227_out, T4);
  and and_225 (and_225_out, Opcode6_9_10, not_217_out, not_228_out, T5);
  and and_226 (and_226_out, Opcode4_5_7_8, INSTRUCTION[2], INSTRUCTION[6], INSTRUCTION[10], T4);
  and and_227 (and_227_out, Opcode4_5_7_8, INSTRUCTION[2], not_218_out, not_219_out, T5);
  and and_228 (and_228_out, Opcode4_5_7_8, not_220_out, INSTRUCTION[6], not_221_out, T5);
  and and_229 (and_229_out, Opcode4_5_7_8, not_222_out, not_223_out, not_224_out, T6);
  and and_230 (and_230_out, Opcode13_14, INSTRUCTION[6], not_229_out, T6);
  and and_231 (and_231_out, Opcode13_14, not_225_out, not_230_out, T6);
  and and_232 (and_232_out, Opcode15, not_231_out, T4);
  and and_233 (and_233_out, T4, Opcode12);
  or or_65 (or_65_out, T1, T3, and_221_out);
  assign FunSelARF = and_233_out ? 2'b00 : 2'bz;  // Controlled_Buffer controlled_buffer_42
  assign FunSelARF = or_65_out ? 2'b01 : 2'bz;  // Controlled_Buffer controlled_buffer_43
  or or_66 (or_66_out, and_222_out, and_223_out, and_224_out, and_225_out, and_226_out, and_228_out, and_229_out, and_230_out, and_231_out, and_232_out, and_227_out);
  assign FunSelARF = or_66_out ? 2'b10 : 2'bz;  // Controlled_Buffer controlled_buffer_44
  not not_232 (not_232_out, INSTRUCTION[10]);
  not not_233 (not_233_out, T0);
  not not_234 (not_234_out, T2);
  and and_234 (and_234_out, Opcode2, T4);
  and and_235 (and_235_out, Opcode11, T5);
  and and_236 (and_236_out, Opcode12, T4);
  and and_237 (and_237_out, Opcode1, not_233_out, not_234_out, not_232_out);
  or or_67 (or_67_out, T0, T2);
  or or_68 (or_68_out, and_237_out, and_234_out);
  or or_69 (or_69_out, and_235_out, and_236_out);
  assign OutDSel = or_67_out ? 2'b00 : 2'bz;  // Controlled_Buffer controlled_buffer_45
  assign OutDSel = or_68_out ? 2'b10 : 2'bz;  // Controlled_Buffer controlled_buffer_46
  assign OutDSel = or_69_out ? 2'b11 : 2'bz;  // Controlled_Buffer controlled_buffer_47

  // Other names for the same wires on the sheet: IR12 = INSTRUCTION[12]; IR13 = INSTRUCTION[13];
  //   IR14 = INSTRUCTION[14]; IR15 = INSTRUCTION[15]; IR8 = INSTRUCTION[8]; IR9 = INSTRUCTION[9];
  //   IR4 = INSTRUCTION[4]; IR5 = INSTRUCTION[5]; IR0 = INSTRUCTION[0]; IR1 = INSTRUCTION[1]; CLK = in_3;
  //   IR2 = INSTRUCTION[2]; IR3 = INSTRUCTION[3]; IR6 = INSTRUCTION[6]; IR7 = INSTRUCTION[7]; IR10 = INSTRUCTION[10];
  //   IR11 = INSTRUCTION[11]

  // Notes on the sheet:
  //   Opcode
  //   MUXA
  //   MUXB
  //   FunSel ALU
  //   OutASel
  //   IR(8-9) DECODED
  //   100
  //   IR(0-3) DECODED
  //   IR(4-7) DECODED
  //   OutBSel
  //   101
  //   100
  //   RegselRF
  //   IR(8-9) DECODED
  //   9 10 DECODED kaldı
  //   IR(8-11) DECODED
  //   TempselRF
  //   1011
  //   1110
  //   0111
  //   OutCSel
  //   RegSelARF
  //   FunSel RF
  //   FunSelARF
  //   OutDSel
endmodule
