// Logisim project Part2-b.circ as structural Verilog: 1 circuit, main circuit main
module main (
  input  CLK,
  input  [7:0] Input,
  input  [1:0] FunSel,
  input  [2:0] RegSel,
  input  [1:0] OutCSel,
  input  [1:0] OutDSel,
  output [7:0] OutC,
  output [7:0] OutD
);

  wire [2:0] not_1_out;
  wire [7:0] AR_output, PC_output, SP_output;

  assign not_1_out = ~RegSel;  // NOT_Gate not_1, 3 bits wide
  Hex_Digit_Display hex_digit_display_1 (.value(Input[7:4]));  // open: dp
  Hex_Digit_Display hex_digit_display_2 (.value(Input[3:0]));  // open: dp
  REGISTER___8_BIT_main PC (.Input(Input), .FunSel(FunSel), .EN(not_1_out[2]), .Output(PC_output), .CLK(CLK));
  REGISTER___8_BIT_main AR (.Input(Input), .FunSel(FunSel), .EN(not_1_out[1]), .Output(AR_output), .CLK(CLK));
  REGISTER___8_BIT_main SP (.Input(Input), .FunSel(FunSel), .EN(not_1_out[0]), .Output(SP_output), .CLK(CLK));
  Multiplexer #(.select(2), .width(8), .enable("false")) multiplexer_1 (
    .in0(PC_output), .in1(PC_output), .in2(AR_output), .in3(SP_output), .out(OutC), .sel(OutCSel));
  Multiplexer #(.select(2), .width(8), .enable("false")) multiplexer_2 (
    .in0(PC_output), .in1(PC_output), .in2(AR_output), .in3(SP_output), .out(OutD), .sel(OutDSel));
  Hex_Digit_Display hex_digit_display_3 (.value(OutC[3:0]));  // open: dp
  Hex_Digit_Display hex_digit_display_4 (.value(OutC[7:4]));  // open: dp
  Hex_Digit_Display hex_digit_display_5 (.value(OutD[7:4]));  // open: dp
  Hex_Digit_Display hex_digit_display_6 (.value(OutD[3:0]));  // open: dp

  // Notes on the sheet:
  //   OutC
  //   OutD
endmodule
