// Logisim project Part2.circ as structural Verilog: 1 circuit, main circuit main
module main (
  input  in_1,
  input  [7:0] Input,
  input  [3:0] RegSel,
  input  [1:0] FunSel,
  input  [3:0] TempSel,
  input  [2:0] OutASel,
  input  [2:0] OutBSel,
  output [7:0] OutA,
  output [7:0] OutB
);

  wire [3:0] not_1_out, not_2_out;
  wire [7:0] R1_output, R2_output, R3_output, R4_output, T1_output, T2_output, T3_output, T4_output;

  Hex_Digit_Display hex_digit_display_1 (.value(Input[7:4]));  // open: dp
  Hex_Digit_Display hex_digit_display_2 (.value(Input[3:0]));  // open: dp
  assign not_1_out = ~RegSel;  // NOT_Gate not_1, 4 bits wide
  REGISTER___8_BIT_main R1 (.Input(Input), .FunSel(FunSel), .EN(not_1_out[3]), .Output(R1_output), .CLK(in_1));
  REGISTER___8_BIT_main R2 (.Input(Input), .FunSel(FunSel), .EN(not_1_out[2]), .Output(R2_output), .CLK(in_1));
  REGISTER___8_BIT_main R3 (.Input(Input), .FunSel(FunSel), .EN(not_1_out[1]), .Output(R3_output), .CLK(in_1));
  REGISTER___8_BIT_main R4 (.Input(Input), .FunSel(FunSel), .EN(not_1_out[0]), .Output(R4_output), .CLK(in_1));
  assign not_2_out = ~TempSel;  // NOT_Gate not_2, 4 bits wide
  Hex_Digit_Display hex_digit_display_3 (.value(OutA[7:4]));  // open: dp
  Hex_Digit_Display hex_digit_display_4 (.value(OutA[3:0]));  // open: dp
  Multiplexer #(.select(3), .width(8), .enable("false")) multiplexer_1 (
    .in0(R1_output), .in1(R2_output), .in2(R3_output), .in3(R4_output), .in4(T1_output), .in5(T2_output),
    .in6(T3_output), .in7(T4_output), .out(OutA), .sel(OutASel));
  REGISTER___8_BIT_main T1 (.Input(Input), .FunSel(FunSel), .EN(not_2_out[3]), .Output(T1_output), .CLK(in_1));
  REGISTER___8_BIT_main T2 (.Input(Input), .FunSel(FunSel), .EN(not_2_out[2]), .Output(T2_output), .CLK(in_1));
  REGISTER___8_BIT_main T3 (.Input(Input), .FunSel(FunSel), .EN(not_2_out[1]), .Output(T3_output), .CLK(in_1));
  REGISTER___8_BIT_main T4 (.Input(Input), .FunSel(FunSel), .EN(not_2_out[0]), .Output(T4_output), .CLK(in_1));
  Multiplexer #(.select(3), .width(8), .enable("false")) multiplexer_2 (
    .in0(R1_output), .in1(R2_output), .in2(R3_output), .in3(R4_output), .in4(T1_output), .in5(T2_output),
    .in6(T3_output), .in7(T4_output), .out(OutB), .sel(OutBSel));
  Hex_Digit_Display hex_digit_display_5 (.value(OutB[7:4]));  // open: dp
  Hex_Digit_Display hex_digit_display_6 (.value(OutB[3:0]));  // open: dp
endmodule
