// Logisim project Register-16bit.circ as structural Verilog: 1 circuit, main circuit main
module main (
  input  [7:0] I,
  input  L_H,
  input  CLK,
  input  E,
  input  [1:0] FunSel,
  output [15:0] Q
);

  wire [7:0] undriven, undriven_2;
  wire [15:0] adder_1_out, multiplexer_1_out, multiplexer_2_out, subtractor_1_out;

  Hex_Digit_Display hex_digit_display_1 (.value(I[7:4]));  // open: dp
  Hex_Digit_Display hex_digit_display_2 (.value(I[3:0]));  // open: dp
  Multiplexer #(.width(16), .enable("false")) multiplexer_1 (
    .in0({I, undriven}), .in1({undriven_2, I}), .out(multiplexer_1_out), .sel(L_H));
  Multiplexer #(.select(2), .width(16)) multiplexer_2 (
    .in0(subtractor_1_out), .in1(adder_1_out), .in2(multiplexer_1_out), .in3({16{1'b0}}),
    .out(multiplexer_2_out), .sel(FunSel), .en(E));
  _16bit_D_Latch_main main_1 (.IN(multiplexer_2_out), .CLR(1'b0), .EN(E), .CLK(CLK), .OUT(Q));
  Hex_Digit_Display hex_digit_display_3 (.value(Q[15:12]));  // open: dp
  Hex_Digit_Display hex_digit_display_4 (.value(Q[7:4]));  // open: dp
  Hex_Digit_Display hex_digit_display_5 (.value(Q[11:8]));  // open: dp
  Adder #(.width(16)) adder_1 (.a(Q), .b(16'h1), .out(adder_1_out));  // open: cin, cout
  Subtractor #(.width(16)) subtractor_1 (.a(Q), .b(16'h1), .out(subtractor_1_out));  // open: bin, bout
  Hex_Digit_Display hex_digit_display_6 (.value(Q[3:0]));  // open: dp

  // Notes on the sheet:
  //    D FLIP FLOP
  //   ADDER
  //   SUBTRACTOR
endmodule
